# Fritzing sketch display-case (saved by Fritzing 0.8.7b)

parts:
  Arduino_Uno = Arduino Uno (Rev3)
  LED1 = LED - 5mm [color="Red (633nm)" package="5 mm [THT]"]
  R1 = Resistor [tolerance=±5% resistance=680 package=THT]
  LEDs = RELAY [part_number="Spatuala Bot" package=relay-g5q]
  U2 = RELAY [part_number="Line Follower" package=relay-g5q]
  U3 = RELAY [part_number=Xylophone package=relay-g5q]
  LEDs_2 = RELAY [part_number="LED Strip" package=relay-g5q]

nets:
  N1: Arduino_Uno.D13/SCK, LED1.anode
  N2: Arduino_Uno.D4, LEDs_2.COIL1
  N3: Arduino_Uno.D5_PWM, U3.COIL1
  N4: Arduino_Uno.D6_PWM, U2.COIL1
  N5: Arduino_Uno.D7, LEDs.COIL1
  5V: Arduino_Uno.5V
  GND: Arduino_Uno.GND, R1.Pin_1, LEDs.COIL2, U2.COIL2, U3.COIL2, LEDs_2.COIL2
